// Logisim project COA_final_project_1.circ as structural Verilog
module register16bit_LSBMSB (
  input  [15:0] Data,
  input  WE,
  input  Clk,
  input  Reset,
  input  OE,
  output [15:0] Result,
  output [15:0] Dout,
  output [7:0] Eight_LSBs,
  output [7:0] Eight_MSBs
);

  Register #(.width(16)) register_1 (.D(Data), .en(WE), .clk(Clk), .Q(Result), .clr(Reset));
  assign Dout = OE ? Result : 16'bz;  // Controlled_Buffer controlled_buffer_1
  BitSelector #(.group(8), .width(16)) bitselector_1 (.in(Dout), .out(Eight_MSBs), .sel(1'b1));
  BitSelector #(.group(8), .width(16)) bitselector_2 (.in(Dout), .out(Eight_LSBs), .sel(1'b0));
endmodule

module register16bits (
  input  [15:0] Data,
  input  WE,
  input  Clk,
  input  Reset,
  output [15:0] Result
);

  Register #(.width(16)) register_1 (.D(Data), .en(WE), .clk(Clk), .Q(Result), .clr(Reset));
endmodule

module datapath (
  input  [15:0] Data_in,
  input  OE,
  input  IR_OE,
  input  MBR_OE,
  input  in_5,
  input  [3:0] AUsel,
  input  MBR_WE,
  input  [2:0] RUsel,
  input  OutReg_WE,
  input  OutReg_OE,
  output [15:0] out_11
);

  wire clock_1_out, clock_2_out;
  wire [7:0] bitselector_1_out, MAR_result;
  wire [15:0] controlled_buffer_1_out, Instruction_Register_result, MBR_result, project_alu_1_out_6,
       Register_A_result, Register_B_result;

  Clock clock_1 (.out(clock_1_out));
  BitSelector #(.group(8), .width(16)) bitselector_1 (
    .in(controlled_buffer_1_out), .out(bitselector_1_out), .sel(1'b1));
  assign controlled_buffer_1_out = IR_OE ? Instruction_Register_result : 16'bz;  // Controlled_Buffer controlled_buffer_1
  register16bits Instruction_Register (
    .Data(project_alu_1_out_6), .Clk(clock_1_out), .Result(Instruction_Register_result));  // open: WE, Reset
  register16bits Register_A (
    .Data(project_alu_1_out_6), .Clk(clock_1_out), .Result(Register_A_result));  // open: WE, Reset
  project_alu project_alu_1 (
    .A(Register_A_result), .B(Register_B_result), .RUsel(RUsel), .AUsel(AUsel), .out_6(project_alu_1_out_6));  // open: RUresult, Auresult
  register16bits Register_B (
    .Data(project_alu_1_out_6), .Clk(clock_1_out), .Result(Register_B_result));  // open: WE, Reset
  assign project_alu_1_out_6 = OE ? Data_in : 16'bz;  // Controlled_Buffer controlled_buffer_2
  assign project_alu_1_out_6 = MBR_OE ? MBR_result : 16'bz;  // Controlled_Buffer controlled_buffer_3
  register8bit MAR (.Data(bitselector_1_out), .Clk(clock_2_out), .Result(MAR_result));  // open: WE, Reset
  register16bits MBR (.WE(MBR_WE), .Data(project_alu_1_out_6), .Clk(clock_2_out), .Result(MBR_result));  // open: Reset
  register16bits Output_Register (
    .WE(OutReg_WE), .Data(project_alu_1_out_6), .Clk(clock_2_out), .Result(out_11));  // open: Reset
  assign project_alu_1_out_6 = OutReg_OE ? out_11 : 16'bz;  // Controlled_Buffer controlled_buffer_4
  Clock clock_2 (.out(clock_2_out));
  assign project_alu_1_out_6 = in_5 ? MBR_result : 16'bz;  // Controlled_Buffer controlled_buffer_5

  // Notes on the sheet:
  //   Datapath
endmodule

module project_ao (
  input  [3:0] AUsel,
  input  [15:0] A,
  input  [15:0] B,
  output [15:0] Auresult
);

  wire [15:0] adder_1_out, and_1_out, divider_1_out, multiplier_1_out, negator_1_out, negator_2_out,
       or_1_out, shifter_1_out, shifter_2_out, shifter_3_out, shifter_4_out, subtractor_1_out, xor_1_out;

  Adder #(.width(16)) adder_1 (.a(A), .b(B), .out(adder_1_out));  // open: cin, cout
  Divider #(.width(16)) divider_1 (.a(A), .b(B), .out(divider_1_out));  // open: upper, rem
  Multiplier #(.width(16)) multiplier_1 (.a(A), .b(B), .out(multiplier_1_out));  // open: cin, cout
  Subtractor #(.width(16)) subtractor_1 (.a(A), .b(B), .out(subtractor_1_out));  // open: bin, bout
  Shifter #(.width(16)) shifter_1 (.in(A), .\dist (4'b0010), .out(shifter_1_out));
  Shifter #(.width(16)) shifter_2 (.in(B), .\dist (4'b0010), .out(shifter_2_out));
  Shifter #(.shift("lr"), .width(16)) shifter_3 (.in(A), .\dist (4'b0010), .out(shifter_3_out));
  Shifter #(.shift("lr"), .width(16)) shifter_4 (.in(B), .\dist (4'b0010), .out(shifter_4_out));
  Negator #(.width(16)) negator_1 (.in(A), .out(negator_1_out));
  Negator #(.width(16)) negator_2 (.in(B), .out(negator_2_out));
  assign and_1_out = A & B;  // AND_Gate and_1, 16 bits wide
  assign or_1_out = A | B;  // OR_Gate or_1, 16 bits wide
  assign xor_1_out = A ^ B;  // XOR_Gate xor_1, 16 bits wide
  Multiplexer #(.select(4), .width(16)) multiplexer_1 (
    .in0(adder_1_out), .in1(and_1_out), .in2(or_1_out), .in3(xor_1_out), .in4(divider_1_out),
    .in5(multiplier_1_out), .in6(subtractor_1_out), .in7(shifter_1_out), .in8(shifter_2_out),
    .in9(shifter_3_out), .in10(shifter_4_out), .in11(negator_1_out), .in12(negator_2_out), .out(Auresult),
    .sel(AUsel));  // open: in13, in14, in15
endmodule

module project_ro (
  input  [15:0] A,
  input  [15:0] B,
  input  [2:0] in_3,
  output RUresult
);

  wire comparator_1_eq, comparator_1_gt, comparator_1_lt, not_1_out, or_1_out, or_2_out;

  Comparator #(.width(16)) comparator_1 (
    .a(A), .b(B), .gt(comparator_1_gt), .eq(comparator_1_eq), .lt(comparator_1_lt));
  or or_1 (or_1_out, comparator_1_gt, comparator_1_eq);
  not not_1 (not_1_out, comparator_1_eq);
  or or_2 (or_2_out, comparator_1_eq, comparator_1_lt);
  Multiplexer #(.select(3)) multiplexer_1 (
    .in0(not_1_out), .in1(comparator_1_eq), .in2(comparator_1_lt), .in3(or_2_out), .in4(comparator_1_gt),
    .in5(or_1_out), .out(RUresult), .sel(in_3));  // open: in6, in7
endmodule

module project_alu (
  input  [3:0] AUsel,
  input  [15:0] A,
  input  [15:0] B,
  input  [2:0] RUsel,
  output [15:0] Auresult,
  output [15:0] out_6,
  output RUresult
);

  project_ao project_ao_1 (.AUsel(AUsel), .A(A), .B(B), .Auresult(Auresult));
  project_ro project_ro_1 (.A(A), .B(B), .in_3(RUsel), .RUresult(RUresult));
  assign out_6 = ~Auresult;  // NOT_Gate not_1, 16 bits wide
endmodule

module register8bit (
  input  [7:0] Data,
  input  WE,
  input  Clk,
  input  Reset,
  output [7:0] Result
);

  Register register_1 (.D(Data), .en(WE), .clk(Clk), .Q(Result), .clr(Reset));
endmodule
